# Fritzing sketch Liting (saved by Fritzing 0.9.1b)
breadboards: 1

parts:
  IC1 = MCP23017 I2C I/O Expander
  Part1 = Arduino Uno (Rev3)
  R1 = Resistor [tolerance=±5% resistance=4.7k package=THT]
  R2 = Resistor [tolerance=±5% resistance=4.7k package=THT]
  ENCODER1 = Rotary Encoder with Knob
  ENCODER2 = Rotary Encoder with Knob
  ENCODER3 = Rotary Encoder with Knob
  ENCODER4 = Rotary Encoder with Knob

nets:
  N1: IC1.GPB0, ENCODER1.no_name_yet#4
  VDD: IC1.VDD, IC1.RESET, Part1.5V, R1.Pin_1, R2.Pin_0
  VSS: IC1.VSS, IC1.A0, IC1.A1, IC1.A2, Part1.GND, ENCODER1.no_name_yet#2, ENCODER1.no_name_yet#5, ENCODER2.no_name_yet#2, ENCODER3.no_name_yet#2, ENCODER4.no_name_yet#2
  N2: IC1.SCL, Part1.A5/SCL, R1.Pin_0
  N3: IC1.SDA, Part1.A4/SDA, R2.Pin_1
  N4: IC1.INTA, Part1.D2
  N5: IC1.GPA0, ENCODER4.no_name_yet#3
  N6: IC1.GPA1, ENCODER4.no_name_yet#1
  N7: IC1.GPA2, ENCODER3.no_name_yet#3
  N8: IC1.GPA3, ENCODER3.no_name_yet#1
  N9: IC1.GPA4, ENCODER2.no_name_yet#3
  N10: IC1.GPA5, ENCODER2.no_name_yet#1
  N11: IC1.GPA6, ENCODER1.no_name_yet#3
  N12: IC1.GPA7, ENCODER1.no_name_yet#1

custom parts:
  MCP23017 I2C I/O Expander: The MCP23017 uses two i2c pins (these can be shared with other i2c devices), and in exchange gives you 16 general purpose pins. You can set each of 16 pins to be input, output, input with a pullup or open drain. There's even the ability to get an interrupt via an external pin when any of the inputs change so you don't have to keep polling the chip.
  Rotary Encoder with Knob: Rotary Encoder with 1/4" Shaft and Knob
